// Logisim project alejandro_caro_project2.circ as structural Verilog
module Leftshift32 (
  input  [4:0] Sa,
  input  [31:0] B,
  input  Cin,
  output [31:0] C
);

  wire [1:0] multiplexer_3_out;
  wire [3:0] bit_extender_3_out, multiplexer_2_out, multiplexer_2_out_2, multiplexer_2_out_3,
       multiplexer_2_out_4, multiplexer_2_out_5, multiplexer_2_out_6, multiplexer_2_out_7,
       multiplexer_2_out_8;
  wire [7:0] bit_extender_2_out, multiplexer_1_out, multiplexer_1_out_2, multiplexer_1_out_3,
       multiplexer_1_out_4;
  wire [15:0] bit_extender_1_out;
  wire [31:0] bit_extender_4_out;
  wire [31:8] multiplexer_4_out_2;
  wire [31:31] multiplexer_4_out;

  assign bit_extender_1_out = {{15{Cin}}, Cin};  // Bit_Extender bit_extender_1
  assign bit_extender_2_out = {{7{Cin}}, Cin};  // Bit_Extender bit_extender_2
  assign bit_extender_3_out = {{3{Cin}}, Cin};  // Bit_Extender bit_extender_3
  Multiplexer #(.width(32)) multiplexer_1 (
    .in0(B), .in1({B[15:0], bit_extender_1_out}),
    .out({multiplexer_1_out, multiplexer_1_out_4, multiplexer_1_out_3, multiplexer_1_out_2}), .sel(Sa[4]));
  Multiplexer #(.width(32)) multiplexer_2 (
    .in0({multiplexer_1_out, multiplexer_1_out_4, multiplexer_1_out_3, multiplexer_1_out_2}),
    .in1({multiplexer_1_out_4, multiplexer_1_out_3, multiplexer_1_out_2, bit_extender_2_out}),
    .out({multiplexer_2_out, multiplexer_2_out_8, multiplexer_2_out_7, multiplexer_2_out_6, multiplexer_2_out_5, multiplexer_2_out_4, multiplexer_2_out_3, multiplexer_2_out_2}),
    .sel(Sa[3]));
  Multiplexer #(.width(32)) multiplexer_3 (
    .in0({multiplexer_2_out, multiplexer_2_out_8, multiplexer_2_out_7, multiplexer_2_out_6, multiplexer_2_out_5, multiplexer_2_out_4, multiplexer_2_out_3, multiplexer_2_out_2}),
    .in1({multiplexer_2_out_8, multiplexer_2_out_7, multiplexer_2_out_6, multiplexer_2_out_5, multiplexer_2_out_4, multiplexer_2_out_3, multiplexer_2_out_2, bit_extender_3_out}),
    .out({multiplexer_3_out, bit_extender_4_out[31:2]}), .sel(Sa[2]));
  assign bit_extender_4_out[1:0] = {{1{Cin}}, Cin};  // Bit_Extender bit_extender_4
  Multiplexer #(.width(32)) multiplexer_4 (
    .in0({multiplexer_3_out, bit_extender_4_out[31:2]}), .in1(bit_extender_4_out),
    .out({multiplexer_4_out[31], multiplexer_4_out_2, {7{multiplexer_4_out_2[8]}}}), .sel(Sa[1]));
  Multiplexer #(.width(32)) multiplexer_5 (
    .in0({multiplexer_4_out[31], multiplexer_4_out_2, {7{multiplexer_4_out_2[8]}}}),
    .in1({multiplexer_4_out_2, {7{multiplexer_4_out_2[8]}}, Cin}), .out(C), .sel(Sa[0]));
endmodule

module Add32 (
  input  [31:0] A,
  input  [31:0] B,
  input  Cin,
  output [31:0] C,
  output V
);

  wire xnor_1_out, xor_1_out;

  xor xor_1 (xor_1_out, C[31], A[31]);
  Adder32_Core adder32_core_1 (.A32(A), .B32(B), .cin(Cin), .C32(C));  // open: cout
  xnor xnor_1 (xnor_1_out, B[31], A[31]);
  and and_1 (V, xor_1_out, xnor_1_out);
endmodule

module FullAdder1Bit (
  input  A,
  input  B,
  input  Cin,
  output S,
  output Cout
);

  wire and_1_out, and_2_out, and_3_out;

  xor xor_1 (S, A, B, Cin);
  and and_1 (and_1_out, A, B);
  and and_2 (and_2_out, A, Cin);
  and and_3 (and_3_out, B, Cin);
  or or_1 (Cout, and_1_out, and_2_out, and_3_out);
endmodule

module Adder4Bit (
  input  Cin,
  input  [3:0] B4,
  input  [3:0] A4,
  output [3:0] S4,
  output Carry
);

  wire fulladder1bit_1_cout, fulladder1bit_2_cout, fulladder1bit_3_cout;

  FullAdder1Bit fulladder1bit_1 (.A(A4[0]), .B(B4[0]), .Cin(Cin), .S(S4[0]), .Cout(fulladder1bit_1_cout));
  FullAdder1Bit fulladder1bit_2 (
    .A(A4[1]), .B(B4[1]), .Cin(fulladder1bit_1_cout), .S(S4[1]), .Cout(fulladder1bit_2_cout));
  FullAdder1Bit fulladder1bit_3 (
    .A(A4[2]), .B(B4[2]), .Cin(fulladder1bit_2_cout), .S(S4[2]), .Cout(fulladder1bit_3_cout));
  FullAdder1Bit fulladder1bit_4 (.A(A4[3]), .B(B4[3]), .Cin(fulladder1bit_3_cout), .S(S4[3]), .Cout(Carry));
endmodule

module Adder16Bit (
  input  [15:0] A16,
  input  [15:0] B16,
  input  Carryin,
  output [15:0] C16,
  output carryout
);

  wire adder4bit_1_p5, adder4bit_2_p5, adder4bit_3_p5;

  // Adder4Bit adder4bit_1: pin names not known; wires that end beside it: A16[3:0], B16[3:0], Carryin, C16[3:0], adder4bit_1_p5
  // Adder4Bit adder4bit_2: pin names not known; wires that end beside it: A16[7:4], B16[7:4], adder4bit_1_p5, C16[7:4], adder4bit_2_p5
  // Adder4Bit adder4bit_3: pin names not known; wires that end beside it: A16[11:8], B16[11:8], adder4bit_2_p5, C16[11:8], adder4bit_3_p5
  // Adder4Bit adder4bit_4: pin names not known; wires that end beside it: A16[15:12], B16[15:12], adder4bit_3_p5, C16[15:12], carryout
endmodule

module Adder32_Core (
  input  [31:0] A32,
  input  [31:0] B32,
  input  cin,
  output [31:0] C32,
  output cout
);

  wire adder16bit_1_carryout;

  Adder16Bit adder16bit_1 (
    .A16(A32[15:0]), .B16(B32[15:0]), .Carryin(cin), .C16(C32[15:0]), .carryout(adder16bit_1_carryout));
  Adder16Bit adder16bit_2 (
    .A16(A32[31:16]), .B16(B32[31:16]), .Carryin(adder16bit_1_carryout), .C16(C32[31:16]), .carryout(cout));
endmodule

module ALU32 (
  input  [31:0] A,
  input  [31:0] B,
  input  [4:0] Sa,
  input  [3:0] Op,
  output [31:0] C,
  output V
);

  wire add32_1_v, subtractor32_1_v;
  wire [0:0] equalscomparator_1_c, not_1_out;
  wire [31:0] add32_1_c, and_1_out, arithmeticrightshift_1_c, greaterthanzero_1_out_2, leftshift32_1_p3,
       lessorequalzero_1_out_2, logicalrightshift_1_c, not_2_out, or_1_out, subtractor32_1_c, xor_1_out;

  // Leftshift32 leftshift32_1: pin names not known; wires that end beside it: B, Sa, leftshift32_1_p3
  Add32 add32_1 (.A(A), .B(B), .C(add32_1_c), .V(add32_1_v));  // open: Cin
  assign and_1_out = A & B;  // AND_Gate and_1, 32 bits wide
  assign or_1_out = A | B;  // OR_Gate or_1, 32 bits wide
  assign xor_1_out = A ^ B;  // XOR_Gate xor_1, 32 bits wide
  LogicalRightShift logicalrightshift_1 (.B(B), .Sa(Sa), .C(logicalrightshift_1_c));
  ArithmeticRightShift arithmeticrightshift_1 (.B(B), .Sa(Sa), .C(arithmeticrightshift_1_c));
  Subtractor32 subtractor32_1 (.B(A), .A(B), .C(subtractor32_1_c), .V(subtractor32_1_v));
  EqualsComparator equalscomparator_1 (.B(A), .A(B), .C(equalscomparator_1_c[0]));
  GreaterThanZero greaterthanzero_1 (.A(A), .out_2(greaterthanzero_1_out_2));
  LessOrEqualZero lessorequalzero_1 (.A(A), .out_2(lessorequalzero_1_out_2));
  not not_1 (not_1_out[0], equalscomparator_1_c[0]);
  assign not_2_out = ~or_1_out;  // NOT_Gate not_2, 32 bits wide
  Multiplexer #(.select(4), .width(32)) multiplexer_1 (
    .in0(leftshift32_1_p3), .in1(leftshift32_1_p3), .in2(add32_1_c), .in3(add32_1_c),
    .in4(logicalrightshift_1_c), .in5(arithmeticrightshift_1_c), .in6(subtractor32_1_c),
    .in7(subtractor32_1_c), .in8(and_1_out), .in9({{31{1'b0}}, equalscomparator_1_c[0]}), .in10(or_1_out),
    .in11({{31{1'b0}}, not_1_out[0]}), .in12(xor_1_out), .in13(greaterthanzero_1_out_2), .in14(not_2_out),
    .in15(lessorequalzero_1_out_2), .out(C), .sel(Op));
  Multiplexer #(.select(4)) multiplexer_2 (
    .in0(1'b0), .in1(1'b0), .in2(add32_1_v), .in3(add32_1_v), .in4(1'b0), .in5(1'b0), .in6(subtractor32_1_v),
    .in7(subtractor32_1_v), .in8(1'b0), .in9(1'b0), .in10(1'b0), .in11(1'b0), .in12(1'b0), .in13(1'b0),
    .in14(1'b0), .in15(1'b0), .out(V), .sel(Op));
endmodule

module LogicalRightShift (
  input  [31:0] B,
  input  [4:0] Sa,
  output [31:0] C
);

  // Leftshift32 leftshift32_1: pin names not known; wires that end beside it: {B[0], B[1], B[2], B[3], B[4], B[5], B[6], B[7], B[8], B[9], B[10], B[11], B[12], B[13], B[14], B[15], B[16], B[17], B[18], B[19], B[20], B[21], B[22], B[23], B[24], B[25], B[26], B[27], B[28], B[29], B[30], B[31]}, Sa, {C[0], C[1], C[2], C[3], C[4], C[5], C[6], C[7], C[8], C[9], C[10], C[11], C[12], C[13], C[14], C[15], C[16], C[17], C[18], C[19], C[20], C[21], C[22], C[23], C[24], C[25], C[26], C[27], C[28], C[29], C[30], C[31]}
endmodule

module ArithmeticRightShift (
  input  [31:0] B,
  input  [4:0] Sa,
  output [31:0] C
);

  // Leftshift32 leftshift32_1: pin names not known; wires that end beside it: {B[0], B[1], B[2], B[3], B[4], B[5], B[6], B[7], B[8], B[9], B[10], B[11], B[12], B[13], B[14], B[15], B[16], B[17], B[18], B[19], B[20], B[21], B[22], B[23], B[24], B[25], B[26], B[27], B[28], B[29], B[30], B[31]}, B[31], Sa, {C[0], C[1], C[2], C[3], C[4], C[5], C[6], C[7], C[8], C[9], C[10], C[11], C[12], C[13], C[14], C[15], C[16], C[17], C[18], C[19], C[20], C[21], C[22], C[23], C[24], C[25], C[26], C[27], C[28], C[29], C[30], C[31]}
endmodule

module Subtractor32 (
  input  [31:0] B,
  input  [31:0] A,
  output [31:0] C,
  output V
);

  wire xor_1_out, xor_2_out;
  wire [31:0] adder_1_out, not_1_out;

  assign not_1_out = ~B;  // NOT_Gate not_1, 32 bits wide
  Adder #(.width(32)) adder_1 (.a(not_1_out), .b(32'h1), .out(adder_1_out));  // open: cin, cout
  Adder32_Core adder32_core_1 (.A32(A), .B32(adder_1_out), .C32(C));  // open: cin, cout
  xor xor_1 (xor_1_out, C[31], A[31]);
  xor xor_2 (xor_2_out, A[31], B[31]);
  and and_1 (V, xor_2_out, xor_1_out);
endmodule

module EqualsComparator (
  input  [31:0] B,
  input  [31:0] A,
  output C
);

  wire [31:0] xnor_1_out;

  assign xnor_1_out = ~(A ^ B);  // XNOR_Gate xnor_1, 32 bits wide
  and and_1 (C, xnor_1_out[0], xnor_1_out[1], xnor_1_out[2], xnor_1_out[3], xnor_1_out[4], xnor_1_out[5], xnor_1_out[6], xnor_1_out[7], xnor_1_out[8], xnor_1_out[9], xnor_1_out[10], xnor_1_out[11], xnor_1_out[12], xnor_1_out[13], xnor_1_out[14], xnor_1_out[15], xnor_1_out[17], xnor_1_out[18], xnor_1_out[19], xnor_1_out[20], xnor_1_out[21], xnor_1_out[22], xnor_1_out[23], xnor_1_out[24], xnor_1_out[25], xnor_1_out[26], xnor_1_out[27], xnor_1_out[28], xnor_1_out[29], xnor_1_out[30], xnor_1_out[31]);
endmodule

module GreaterThanZero (
  input  [31:0] A,
  output [31:0] out_2
);

  wire not_1_out, or_1_out;

  or or_1 (or_1_out, A[31], A[30], A[29], A[28], A[27], A[26], A[25], A[24], A[23], A[22], A[21], A[20], A[19], A[18], A[17], A[16], A[14], A[13], A[12], A[11], A[10], A[9], A[8], A[7], A[6], A[5], A[4], A[3], A[2], A[1], A[0], A[15]);
  not not_1 (not_1_out, A[31]);
  and and_1 (out_2[0], or_1_out, not_1_out);

  assign out_2[31:1] = {31{1'b0}};
endmodule

module LessOrEqualZero (
  input  [31:0] A,
  output [31:0] out_2
);

  wire and_1_out, not_1_out, or_1_out;

  or or_1 (or_1_out, A[31], A[30], A[29], A[28], A[27], A[26], A[25], A[24], A[23], A[22], A[21], A[20], A[19], A[18], A[17], A[16], A[14], A[13], A[12], A[11], A[10], A[9], A[8], A[7], A[6], A[5], A[4], A[3], A[2], A[1], A[0], A[15]);
  not not_1 (not_1_out, A[31]);
  not not_2 (out_2[0], and_1_out);
  and and_1 (and_1_out, or_1_out, not_1_out);

  assign out_2[31:1] = {31{1'b0}};
endmodule
